// Digital circuit Computer.dig as structural Verilog
module Computer (
  input  clk
);

  wire ALU, alu_1_carry, Carry, CLK_t, decoder_1_out_15, demultiplexer_1_out_0, demultiplexer_1_out_1,
       demultiplexer_2_out_13, HLT, JMP, LD, LDCTR, LDREGA, not_1_out, pulldown_1_out, reset_1_out;
  wire [3:0] IBottom;
  wire [7:4] Instruction;
  wire [31:0] A, B, C, CTR, D, Data, JMPDST, ld_1_rega, ld_1_regb, REGA, REGB, REGC, REGD;

  ROM #(.bigEndian("true"), .AddrBits(24), .isProgramMemory("true"), .Bits(40), .generic("this.AddrBits=args.bits; this.Bits=args.bits+8;")) rom_1 (
    .A(CTR[23:0]), .sel(1'b1), .D({Data, Instruction, IBottom}));
  Register #(.Bits(32), .generic("this.Bits = args.bits;")) u_A (.D(REGA), .C(CLK_t), .en(LDREGA), .Q(A));
  Register #(.Bits(32), .generic("this.Bits = args.bits;")) u_B (.D(REGB), .C(CLK_t), .en(LDREGA), .Q(B));
  Register #(.Bits(32), .generic("this.Bits = args.bits;")) u_C (.D(REGC), .C(CLK_t), .en(LD), .Q(C));
  Register #(.Bits(32), .generic("this.Bits = args.bits;")) u_D (.D(REGD), .C(CLK_t), .en(LD), .Q(D));
  // Probe CTR on CTR
  // Probe on A
  // Probe on B
  // Probe on C
  // Probe on D
  // Probe on Carry
  // Probe on CTR
  // Probe on A
  // Probe on B
  // Probe on C
  // Probe on D
  // Probe on Carry
  LD #(.generic("bits := args.bits;")) ld_1 (
    .A(A), .B(B), .C(C), .D(D), .Data(Data), .Enable(LD), .Instruction(IBottom), .REGA(ld_1_rega),
    .REGB(ld_1_regb), .REGC(REGC), .REGD(REGD));
  // Probe Instruction on {Instruction, IBottom}
  // Probe Data on Data
  // Probe on {Instruction, IBottom}
  // Probe on Data
  ALU #(.generic("bits := args.bits;")) alu_1 (
    .A(ld_1_rega), .B(ld_1_regb), .Data(Data), .Enable(ALU), .Instruction(IBottom), .CarryIn(Carry),
    .REGA(REGA), .REGB(REGB), .Carry(alu_1_carry));
  Demultiplexer demultiplexer_1 (
    .sel(not_1_out), .in(ALU), .out_0(demultiplexer_1_out_0), .out_1(demultiplexer_1_out_1));
  or or_1 (LDREGA, LD, ALU);
  RS_FF_AS rs_ff_as_1 (.S(demultiplexer_1_out_0), .R(demultiplexer_1_out_1), .Q(Carry));  // open: nQ
  not not_1 (not_1_out, alu_1_carry);
  JMP #(.generic("bits := args.bits;")) jmp_1 (
    .A(REGA), .B(REGB), .Data(Data), .Enable(JMP), .Instruction(IBottom), .Carry(alu_1_carry),
    .Counter(JMPDST), .JMP(LDCTR));
  PullDown pulldown_1 (.out(pulldown_1_out));
  Decoder #(.Selector_Bits(4)) decoder_1 (
    .sel(Instruction), .out_0(LD), .out_1(ALU), .out_2(JMP), .out_15(decoder_1_out_15));  // open: out_3, out_4, out_5, out_6, out_7, out_8, out_9, out_10, out_11, out_12, out_13, out_14
  // Probe CLK on clk
  or or_2 (CLK_t, HLT, clk);
  Reset #(.invertOutput("false")) reset_1 (.out(reset_1_out));
  CounterPreset #(.Bits(32), .isProgramCounter("true"), .generic("this.Bits=args.bits;")) Program_Counter (
    .en(1'b1), .C(CLK_t), .dir(pulldown_1_out), .in(JMPDST), .ld(LDCTR), .clr(reset_1_out), .out(CTR));  // open: ovf
  Demultiplexer #(.Selector_Bits(4)) demultiplexer_2 (
    .sel(IBottom), .in(decoder_1_out_15), .out_13(demultiplexer_2_out_13), .out_15(HLT));  // open: out_0, out_1, out_2, out_3, out_4, out_5, out_6, out_7, out_8, out_9, out_10, out_11, out_12, out_14
  Break break_1 (.brk(demultiplexer_2_out_13));
  // Pins of 24 and 32 bits meet at CTR

  // Other names for the same wires on the sheet: Instruction[3:0] = IBottom; ITop[3:0] = Instruction; LDREGB = LDREGA;
  //   LDREGC = LD; LDREGD = LD

  // Notes on the sheet:
  //   clk: Hz: 100
  //   Read ROM
  //   contents of rom_1 (hex, n*v repeats v):
  //   ffffff01,ff02,ff0003,ff000000,604,ff,705,f000000a,ff000706,30a
  //   ,10*0,504
endmodule

/* Code that sets the parameters or builds the circuit:
bits := 32;
*/
